// Logisim project riscv.circ as structural Verilog: 5 circuits, main circuit main
module main (
);


  // Notes on the sheet:
  //   MAIN CIRCUIT
endmodule

module CU (
);


  // Notes on the sheet:
  //   CONTROL UNIT
endmodule

module ALU (
);


  // Notes on the sheet:
  //   ARITHMETIC AND LOGIC UNIT
endmodule

module RF (
);


  // Notes on the sheet:
  //   REGISTER FIELD
endmodule

module MU (
  input  [15:0] IN_ADDRESS,
  input  [31:0] OUT_DATA,
  input  [31:0] IN_DATA,
  input  WRITE_ENABLE,
  input  CLEAR,
  input  CLOCK,
  input  READ_ENABLE
);

  RAM #(.addrWidth(16), .dataWidth(32), .bus("separate")) ram_1 (
    .addr(IN_ADDRESS), .din(IN_DATA), .data(OUT_DATA), .str(WRITE_ENABLE), .sel(1'b1), .clk(CLOCK),
    .ld(READ_ENABLE), .clr(CLEAR));

  // Notes on the sheet:
  //   MEMORY UNIT
endmodule
